// Logisim project ALU.circ as structural Verilog: 14 circuits, main circuit CPU
module main (
  input  SUB,
  input  W_C,
  input  CAR_I,
  input  LOG_EN,
  input  LOG_SEL_1,
  input  LOG_SEL_0,
  input  RR_0,
  input  D_0,
  input  RR_1,
  input  D_1,
  input  RR_2,
  input  D_2,
  input  RR_3,
  input  D_3,
  output OUT_0,
  output OUT_1,
  output OUT_2,
  output OUT_3,
  output CAR_O
);

  wire and_1_out, and_2_out, and_3_out, and_4_out, and_5_out, and_6_out, and_7_out, and_8_out, and_9_out,
       and_10_out, and_11_out, and_12_out, and_13_out, and_14_out, and_15_out, and_16_out, and_17_out,
       and_18_out, and_20_out, and_21_out, and_22_out, and_23_out, and_24_out, and_25_out, and_26_out,
       and_27_out, and_28_out, and_29_out, and_30_out, and_31_out, and_32_out, and_33_out, and_34_out,
       and_35_out, and_36_out, and_37_out, and_38_out, not_1_out, not_2_out, not_3_out, not_4_out, or_1_out,
       or_2_out, or_3_out, or_4_out, or_5_out, or_6_out, or_7_out, or_8_out, or_9_out, or_10_out, or_11_out,
       or_12_out, or_13_out, or_14_out, or_15_out, or_16_out, or_17_out, xor_1_out, xor_2_out, xor_3_out,
       xor_4_out, xor_5_out, xor_6_out, xor_7_out, xor_8_out, xor_9_out, xor_10_out, xor_11_out, xor_12_out,
       xor_13_out, xor_14_out, xor_15_out, xor_16_out;

  xor xor_1 (xor_1_out, D_0, SUB);
  and and_1 (and_1_out, SUB, not_1_out);
  xor xor_2 (xor_2_out, D_1, SUB);
  xor xor_3 (xor_3_out, D_2, SUB);
  xor xor_4 (xor_4_out, D_3, SUB);
  not not_1 (not_1_out, W_C);
  or or_1 (or_1_out, and_1_out, and_2_out);
  and and_2 (and_2_out, W_C, CAR_I);
  xor xor_5 (xor_5_out, RR_0, xor_1_out);
  xor xor_6 (xor_6_out, RR_1, xor_2_out);
  xor xor_7 (xor_7_out, RR_2, xor_3_out);
  xor xor_8 (xor_8_out, RR_3, xor_4_out);
  xor xor_9 (xor_9_out, xor_5_out, or_1_out);
  and and_3 (and_3_out, xor_5_out, or_1_out);
  and and_4 (and_4_out, RR_0, xor_1_out);
  xor xor_10 (xor_10_out, xor_6_out, or_6_out);
  and and_5 (and_5_out, xor_6_out, or_6_out);
  and and_6 (and_6_out, RR_1, xor_2_out);
  xor xor_11 (xor_11_out, xor_7_out, or_7_out);
  and and_7 (and_7_out, xor_7_out, or_7_out);
  and and_8 (and_8_out, RR_2, xor_3_out);
  xor xor_12 (xor_12_out, xor_8_out, or_8_out);
  and and_9 (and_9_out, xor_8_out, or_8_out);
  and and_10 (and_10_out, RR_3, xor_4_out);
  and and_11 (and_11_out, RR_0, D_0);
  and and_12 (and_12_out, RR_1, D_1);
  and and_13 (and_13_out, RR_2, D_2);
  and and_14 (and_14_out, RR_3, D_3);
  or or_2 (or_2_out, RR_0, D_0);
  or or_3 (or_3_out, RR_1, D_1);
  or or_4 (or_4_out, RR_2, D_2);
  or or_5 (or_5_out, RR_3, D_3);
  xor xor_13 (xor_13_out, RR_0, D_0);
  xor xor_14 (xor_14_out, RR_1, D_1);
  xor xor_15 (xor_15_out, RR_2, D_2);
  xor xor_16 (xor_16_out, RR_3, D_3);
  or or_6 (or_6_out, and_3_out, and_4_out);
  or or_7 (or_7_out, and_5_out, and_6_out);
  or or_8 (or_8_out, and_7_out, and_8_out);
  or or_9 (or_9_out, and_9_out, and_10_out);
  not not_2 (not_2_out, LOG_EN);
  and and_15 (and_15_out, xor_9_out, not_2_out);
  and and_16 (and_16_out, xor_10_out, not_2_out);
  and and_17 (and_17_out, xor_11_out, not_2_out);
  and and_18 (and_18_out, xor_12_out, not_2_out);
  and and_19 (CAR_O, or_9_out, not_2_out);
  and and_20 (and_20_out, and_11_out, and_34_out);
  and and_21 (and_21_out, and_12_out, and_34_out);
  and and_22 (and_22_out, and_13_out, and_34_out);
  and and_23 (and_23_out, and_14_out, and_34_out);
  and and_24 (and_24_out, or_2_out, and_33_out);
  and and_25 (and_25_out, or_3_out, and_33_out);
  and and_26 (and_26_out, or_4_out, and_33_out);
  and and_27 (and_27_out, or_5_out, and_33_out);
  and and_28 (and_28_out, xor_13_out, and_32_out);
  and and_29 (and_29_out, xor_14_out, and_32_out);
  and and_30 (and_30_out, xor_15_out, and_32_out);
  and and_31 (and_31_out, xor_16_out, and_32_out);
  and and_32 (and_32_out, LOG_SEL_1, not_3_out);
  not not_3 (not_3_out, LOG_SEL_0);
  not not_4 (not_4_out, LOG_SEL_1);
  and and_33 (and_33_out, not_4_out, not_3_out);
  and and_34 (and_34_out, not_4_out, LOG_SEL_0);
  or or_10 (or_10_out, and_20_out, and_24_out);
  or or_11 (or_11_out, and_21_out, and_25_out);
  or or_12 (or_12_out, and_22_out, and_26_out);
  or or_13 (or_13_out, and_23_out, and_27_out);
  or or_14 (or_14_out, or_10_out, and_28_out);
  or or_15 (or_15_out, or_11_out, and_29_out);
  or or_16 (or_16_out, or_12_out, and_30_out);
  or or_17 (or_17_out, or_13_out, and_31_out);
  and and_35 (and_35_out, or_14_out, LOG_EN);
  and and_36 (and_36_out, or_15_out, LOG_EN);
  and and_37 (and_37_out, or_16_out, LOG_EN);
  and and_38 (and_38_out, or_17_out, LOG_EN);
  or or_18 (OUT_0, and_15_out, and_35_out);
  or or_19 (OUT_1, and_16_out, and_36_out);
  or or_20 (OUT_2, and_17_out, and_37_out);
  or or_21 (OUT_3, and_18_out, and_38_out);
endmodule

module CPU (
  input  EF0,
  input  EF1,
  input  D0,
  input  D1,
  input  D2,
  input  D3,
  input  RST,
  input  CLK,
  output O_D0_RR0,
  output O_D1_RR1,
  output O_D2_RR2,
  output O_D3_RR3,
  output O_4_MAR,
  output O_5_WRITE,
  output O_6_JMP,
  output O_7_I
);

  wire and_1_out, and_2_out, and_3_out, and_4_out, and_5_out, and_6_out, and_7_out, and_8_out, and_9_out,
       and_10_out, and_11_out, and_12_out, and_13_out, and_14_out, and_15_out, and_16_out, and_17_out,
       and_18_out, and_19_out, and_20_out, and_21_out, and_22_out, and_23_out, and_24_out, and_25_out,
       and_26_out, and_27_out, and_28_out, and_29_out, and_30_out, and_31_out, and_32_out, and_33_out,
       and_34_out, and_35_out, and_36_out, and_37_out, and_38_out, and_39_out, and_40_out, and_41_out,
       and_42_out, and_43_out, and_44_out, and_45_out, and_46_out, clock_gen_2_1_clk1, clock_gen_2_1_clk2,
       clock_gen_2_1_o_s, d_ff_1_q, d_ff_2_q, d_ff_2_qn, d_ff_3_q, d_ff_4_q, d_ff_5_q, d_ff_6_q, d_ff_7_q,
       d_ff_8_q, d_ff_9_q, d_ff_10_q, d_ff_11_q, d_ff_12_q, d_ff_13_q, d_ff_14_q, d_ff_15_q, d_ff_16_q,
       d_ff_17_q, d_ff_18_q, d_ff_19_q, d_ff_20_q, d_ff_21_q, d_ff_22_q, d_ff_23_q, d_ff_24_q, d_ff_25_q,
       d_ff_26_q, d_ff_27_q, dest_reg_sel_new_1_s0, dest_reg_sel_new_1_s1, dest_reg_sel_new_1_s2,
       eq_0_1_is_zero, inst_dec_1_ari, inst_dec_1_i0, inst_dec_1_i1, inst_dec_1_i2, inst_dec_1_i3,
       inst_dec_1_jmp, inst_dec_1_ld, inst_dec_1_ldd, inst_dec_1_log, inst_dec_1_sei, inst_dec_1_smh,
       inst_dec_1_sml, inst_dec_1_str, inst_dec_1_w_car, int_memory_1_do0, int_memory_1_do1,
       int_memory_1_do2, int_memory_1_do3, main_1_car_o, main_1_out_0, main_1_out_1, main_1_out_2,
       main_1_out_3, nor_1_out, not_1_out, not_2_out, not_3_out, not_4_out, not_5_out, not_6_out, not_7_out,
       or_1_out, or_2_out, or_3_out, or_4_out, or_5_out, or_6_out, or_7_out, or_8_out, or_9_out, or_10_out,
       or_11_out, or_12_out, or_13_out, or_14_out;

  and and_1 (and_1_out, clock_gen_2_1_clk2, not_1_out);
  D_Flip_Flop d_ff_1 (.D(and_1_out), .clk(CLK), .Q(d_ff_1_q), .reset(and_9_out));  // open: Qn, preset
  and and_2 (and_2_out, and_44_out, EF0);
  and and_3 (and_3_out, and_44_out, EF1);
  and and_4 (and_4_out, not_5_out, D0);
  and and_5 (and_5_out, not_5_out, D1);
  and and_6 (and_6_out, not_5_out, D2);
  and and_7 (and_7_out, not_5_out, D3);
  not not_1 (not_1_out, inst_dec_1_ldd);
  not not_2 (not_2_out, and_1_out);
  or or_1 (or_1_out, int_memory_1_do1, and_3_out);
  D_Flip_Flop d_ff_2 (
    .D(inst_dec_1_sei), .clk(and_8_out), .Q(d_ff_2_q), .Qn(d_ff_2_qn), .reset(and_9_out));  // open: preset
  and and_8 (and_8_out, d_ff_1_q, not_2_out);
  and and_9 (and_9_out, RST, CLK);
  or or_2 (or_2_out, int_memory_1_do0, and_2_out);
  inst_dec inst_dec_1 (
    .D0(D0), .D1(D1), .D2(D2), .D3(D3), .CLK1(clock_gen_2_1_clk1), .RST_C(and_9_out), .SMH(inst_dec_1_smh),
    .LOG(inst_dec_1_log), .LD(inst_dec_1_ld), .STR(inst_dec_1_str), .SEI(inst_dec_1_sei),
    .SML(inst_dec_1_sml), .ARI(inst_dec_1_ari), .W_CAR(inst_dec_1_w_car), .I0(inst_dec_1_i0),
    .I1(inst_dec_1_i1), .I2(inst_dec_1_i2), .I3(inst_dec_1_i3), .JMP(inst_dec_1_jmp), .LDD(inst_dec_1_ldd));
  // NoConnect on inst_dec_1_i2
  // NoConnect on inst_dec_1_i3
  clock_gen_2 clock_gen_2_1 (
    .RST(RST), .CLK(CLK), .RST_C(and_9_out), .O_S(clock_gen_2_1_o_s), .CLK1(clock_gen_2_1_clk1),
    .CLK2(clock_gen_2_1_clk2));
  or or_3 (or_3_out, or_2_out, and_4_out);
  or or_4 (or_4_out, or_1_out, and_5_out);
  or or_5 (or_5_out, int_memory_1_do2, and_6_out);
  or or_6 (or_6_out, int_memory_1_do3, and_7_out);
  or or_7 (or_7_out, inst_dec_1_sml, inst_dec_1_smh);
  or or_8 (or_8_out, inst_dec_1_log, inst_dec_1_ari);
  main main_1 (
    .SUB(inst_dec_1_i0), .W_C(inst_dec_1_w_car), .CAR_I(d_ff_7_q), .LOG_EN(inst_dec_1_log),
    .LOG_SEL_1(inst_dec_1_i1), .LOG_SEL_0(inst_dec_1_i0), .RR_0(and_12_out), .D_0(or_3_out),
    .RR_1(and_13_out), .D_1(or_4_out), .RR_2(and_14_out), .D_2(or_5_out), .RR_3(and_15_out), .D_3(or_6_out),
    .OUT_0(main_1_out_0), .OUT_1(main_1_out_1), .OUT_2(main_1_out_2), .OUT_3(main_1_out_3),
    .CAR_O(main_1_car_o));
  and and_10 (and_10_out, clock_gen_2_1_clk2, or_8_out);
  and and_11 (and_11_out, clock_gen_2_1_clk2, inst_dec_1_ari);
  and and_12 (and_12_out, d_ff_3_q, not_3_out);
  and and_13 (and_13_out, d_ff_4_q, not_3_out);
  and and_14 (and_14_out, d_ff_5_q, not_3_out);
  and and_15 (and_15_out, d_ff_6_q, not_3_out);
  not not_3 (not_3_out, inst_dec_1_ld);
  D_Flip_Flop d_ff_3 (.D(main_1_out_0), .clk(and_10_out), .Q(d_ff_3_q));  // open: Qn, preset, reset
  D_Flip_Flop d_ff_4 (.D(main_1_out_1), .clk(and_10_out), .Q(d_ff_4_q));  // open: Qn, preset, reset
  D_Flip_Flop d_ff_5 (.D(main_1_out_2), .clk(and_10_out), .Q(d_ff_5_q));  // open: Qn, preset, reset
  D_Flip_Flop d_ff_6 (.D(main_1_out_3), .clk(and_10_out), .Q(d_ff_6_q));  // open: Qn, preset, reset
  D_Flip_Flop d_ff_7 (.D(main_1_car_o), .clk(and_11_out), .Q(d_ff_7_q), .reset(and_9_out));  // open: Qn, preset
  nor nor_1 (nor_1_out, inst_dec_1_i0, inst_dec_1_i1);
  and and_16 (and_16_out, inst_dec_1_i0, d_ff_7_q);
  and and_17 (and_17_out, inst_dec_1_i1, eq_0_1_is_zero);
  and and_18 (and_18_out, nor_1_out, inst_dec_1_jmp);
  and and_19 (and_19_out, inst_dec_1_jmp, and_16_out);
  and and_20 (and_20_out, inst_dec_1_jmp, and_17_out);
  or or_9 (or_9_out, and_18_out, and_19_out);
  and and_21 (and_21_out, d_ff_3_q, d_ff_2_qn);
  and and_22 (and_22_out, d_ff_4_q, d_ff_2_qn);
  and and_23 (and_23_out, d_ff_5_q, d_ff_2_qn);
  and and_24 (and_24_out, d_ff_6_q, d_ff_2_qn);
  or or_10 (or_10_out, or_9_out, and_20_out);
  eq_0 eq_0_1 (.D0(d_ff_3_q), .D1(d_ff_4_q), .D2(d_ff_5_q), .D3(d_ff_6_q), .is_zero(eq_0_1_is_zero));
  dest_reg_sel_new dest_reg_sel_new_1 (
    .CLK1(clock_gen_2_1_clk1), .LDD(inst_dec_1_ldd), .RST(RST), .S0(dest_reg_sel_new_1_s0),
    .S1(dest_reg_sel_new_1_s1), .S2(dest_reg_sel_new_1_s2));
  or or_11 (or_11_out, and_21_out, and_25_out);
  and and_25 (and_25_out, d_ff_2_q, or_3_out);
  or or_12 (or_12_out, and_22_out, and_26_out);
  or or_13 (or_13_out, and_23_out, and_27_out);
  and and_26 (and_26_out, d_ff_2_q, or_4_out);
  and and_27 (and_27_out, d_ff_2_q, or_5_out);
  or or_14 (or_14_out, and_24_out, and_31_out);
  not not_4 (not_4_out, clock_gen_2_1_clk1);
  and and_28 (and_28_out, inst_dec_1_ldd, dest_reg_sel_new_1_s0);
  and and_29 (and_29_out, inst_dec_1_ldd, dest_reg_sel_new_1_s1);
  and and_30 (and_30_out, inst_dec_1_ldd, dest_reg_sel_new_1_s2);
  and and_31 (and_31_out, d_ff_2_q, or_6_out);
  and and_32 (and_32_out, inst_dec_1_sml, not_4_out);
  and and_33 (and_33_out, inst_dec_1_smh, not_4_out);
  and and_34 (and_34_out, clock_gen_2_1_clk2, and_28_out);
  and and_35 (and_35_out, clock_gen_2_1_clk2, and_29_out);
  and and_36 (and_36_out, clock_gen_2_1_clk2, and_30_out);
  D_Flip_Flop d_ff_8 (.D(or_11_out), .clk(and_32_out), .Q(d_ff_8_q), .reset(and_9_out));  // open: Qn, preset
  D_Flip_Flop d_ff_9 (.D(or_12_out), .clk(and_32_out), .Q(d_ff_9_q), .reset(and_9_out));  // open: Qn, preset
  D_Flip_Flop d_ff_10 (.D(or_13_out), .clk(and_32_out), .Q(d_ff_10_q), .reset(and_9_out));  // open: Qn, preset
  D_Flip_Flop d_ff_11 (.D(or_14_out), .clk(and_32_out), .Q(d_ff_11_q), .reset(and_9_out));  // open: Qn, preset
  D_Flip_Flop d_ff_12 (.D(or_11_out), .clk(and_33_out), .Q(d_ff_12_q), .reset(and_9_out));  // open: Qn, preset
  D_Flip_Flop d_ff_13 (.D(or_12_out), .clk(and_33_out), .Q(d_ff_13_q), .reset(and_9_out));  // open: Qn, preset
  D_Flip_Flop d_ff_14 (.D(or_13_out), .clk(and_33_out), .Q(d_ff_14_q), .reset(and_9_out));  // open: Qn, preset
  D_Flip_Flop d_ff_15 (.D(or_14_out), .clk(and_33_out), .Q(d_ff_15_q), .reset(and_9_out));  // open: Qn, preset
  D_Flip_Flop d_ff_16 (.D(or_11_out), .clk(and_34_out), .Q(d_ff_16_q));  // open: Qn, preset, reset
  D_Flip_Flop d_ff_17 (.D(or_12_out), .clk(and_34_out), .Q(d_ff_17_q));  // open: Qn, preset, reset
  D_Flip_Flop d_ff_18 (.D(or_13_out), .clk(and_34_out), .Q(d_ff_18_q));  // open: Qn, preset, reset
  D_Flip_Flop d_ff_19 (.D(or_14_out), .clk(and_34_out), .Q(d_ff_19_q));  // open: Qn, preset, reset
  D_Flip_Flop d_ff_20 (.D(or_11_out), .clk(and_35_out), .Q(d_ff_20_q));  // open: Qn, preset, reset
  D_Flip_Flop d_ff_21 (.D(or_12_out), .clk(and_35_out), .Q(d_ff_21_q));  // open: Qn, preset, reset
  D_Flip_Flop d_ff_22 (.D(or_13_out), .clk(and_35_out), .Q(d_ff_22_q));  // open: Qn, preset, reset
  D_Flip_Flop d_ff_23 (.D(or_14_out), .clk(and_35_out), .Q(d_ff_23_q));  // open: Qn, preset, reset
  D_Flip_Flop d_ff_24 (.D(or_11_out), .clk(and_36_out), .Q(d_ff_24_q));  // open: Qn, preset, reset
  D_Flip_Flop d_ff_25 (.D(or_12_out), .clk(and_36_out), .Q(d_ff_25_q));  // open: Qn, preset, reset
  D_Flip_Flop d_ff_26 (.D(or_13_out), .clk(and_36_out), .Q(d_ff_26_q));  // open: Qn, preset, reset
  D_Flip_Flop d_ff_27 (.D(or_14_out), .clk(and_36_out), .Q(d_ff_27_q));  // open: Qn, preset, reset
  and and_37 (and_37_out, inst_dec_1_str, not_6_out);
  output_logic output_logic_1 (
    .O_S(clock_gen_2_1_o_s), .DO_JMP(or_10_out), .DEST_0(d_ff_16_q), .DEST_1(d_ff_17_q), .DEST_2(d_ff_18_q),
    .DEST_3(d_ff_19_q), .DEST_4(d_ff_20_q), .DEST_5(d_ff_21_q), .DEST_6(d_ff_22_q), .DEST_7(d_ff_23_q),
    .MAR_0(d_ff_8_q), .MAR_1(d_ff_9_q), .MAR_2(d_ff_10_q), .MAR_3(d_ff_11_q), .MAR_4(d_ff_12_q),
    .MAR_5(d_ff_13_q), .MAR_6(d_ff_14_q), .MAR_7(d_ff_15_q), .DEST_8(d_ff_24_q), .DEST_9(d_ff_25_q),
    .DEST_10(d_ff_26_q), .DEST_11(d_ff_27_q), .RR_0(d_ff_3_q), .RR_1(d_ff_4_q), .RR_2(d_ff_5_q),
    .RR_3(d_ff_6_q), .MAR(or_7_out), .WRITE(and_37_out), .JMP(or_10_out), .F_I(d_ff_2_q), .OUT_0(O_D0_RR0),
    .OUT_1(O_D1_RR1), .OUT_2(O_D2_RR2), .OUT_3(O_D3_RR3), .OUT_4(O_4_MAR), .OUT_5(O_5_WRITE),
    .OUT_6(O_6_JMP), .OUT_7(O_7_I));
  and and_38 (and_38_out, d_ff_8_q, d_ff_9_q);
  and and_39 (and_39_out, d_ff_10_q, d_ff_11_q);
  and and_40 (and_40_out, d_ff_12_q, d_ff_13_q);
  and and_41 (and_41_out, d_ff_14_q, d_ff_15_q);
  and and_42 (and_42_out, and_38_out, and_39_out);
  and and_43 (and_43_out, and_40_out, and_41_out);
  and and_44 (and_44_out, and_42_out, and_45_out);
  and and_45 (and_45_out, and_43_out, d_ff_2_qn);
  not not_5 (not_5_out, and_45_out);
  not not_6 (not_6_out, and_46_out);
  not not_7 (not_7_out, and_44_out);
  int_memory int_memory_1 (
    .ADR0(d_ff_8_q), .ADR1(d_ff_9_q), .ADR2(d_ff_10_q), .ADR3(d_ff_11_q), .DI0(d_ff_3_q), .DI1(d_ff_4_q),
    .DI2(d_ff_5_q), .DI3(d_ff_6_q), .EN(and_46_out), .WR(inst_dec_1_str), .CLK(CLK), .DO0(int_memory_1_do0),
    .DO1(int_memory_1_do1), .DO2(int_memory_1_do2), .DO3(int_memory_1_do3));
  and and_46 (and_46_out, not_7_out, and_45_out);

  // Notes on the sheet:
  //   ~F_I
  //   F_I
  //   MAR LOW
  //   MAR HIGH
  //   DEST 0
  //   DEST 4
  //   DEST 8
endmodule

module eq_0 (
  input  D0,
  input  D1,
  input  D2,
  input  D3,
  output is_zero
);

  wire or_1_out, or_2_out;

  or or_1 (or_1_out, D0, D1);
  or or_2 (or_2_out, D2, D3);
  nor nor_1 (is_zero, or_1_out, or_2_out);
endmodule

module output_logic (
  input  O_S,
  input  DO_JMP,
  input  DEST_0,
  input  DEST_1,
  input  DEST_2,
  input  DEST_3,
  input  DEST_4,
  input  DEST_5,
  input  DEST_6,
  input  DEST_7,
  input  MAR_0,
  input  MAR_1,
  input  MAR_2,
  input  MAR_3,
  input  MAR_4,
  input  MAR_5,
  input  MAR_6,
  input  MAR_7,
  input  DEST_8,
  input  DEST_9,
  input  DEST_10,
  input  DEST_11,
  input  RR_0,
  input  RR_1,
  input  RR_2,
  input  RR_3,
  input  MAR,
  input  WRITE,
  input  JMP,
  input  F_I,
  output OUT_0,
  output OUT_1,
  output OUT_2,
  output OUT_3,
  output OUT_4,
  output OUT_5,
  output OUT_6,
  output OUT_7
);

  wire and_1_out, and_2_out, and_3_out, and_4_out, and_5_out, and_6_out, and_7_out, and_8_out, and_9_out,
       and_10_out, and_11_out, and_12_out, and_13_out, and_14_out, and_15_out, and_16_out, and_17_out,
       and_18_out, and_19_out, and_20_out, and_21_out, and_22_out, and_23_out, and_24_out, and_25_out,
       and_26_out, and_27_out, and_28_out, and_29_out, and_30_out, and_31_out, and_32_out, and_33_out,
       and_34_out, and_35_out, and_36_out, and_37_out, and_38_out, and_39_out, and_40_out, not_1_out,
       not_2_out, or_1_out, or_2_out, or_3_out, or_4_out, or_5_out, or_6_out, or_7_out, or_8_out, or_9_out,
       or_10_out, or_11_out, or_12_out;

  not not_1 (not_1_out, DO_JMP);
  and and_1 (and_1_out, DEST_0, DO_JMP);
  and and_2 (and_2_out, DEST_1, DO_JMP);
  and and_3 (and_3_out, DEST_2, DO_JMP);
  and and_4 (and_4_out, DEST_3, DO_JMP);
  and and_5 (and_5_out, DEST_4, DO_JMP);
  and and_6 (and_6_out, DEST_5, DO_JMP);
  and and_7 (and_7_out, DEST_6, DO_JMP);
  and and_8 (and_8_out, DEST_7, DO_JMP);
  and and_9 (and_9_out, MAR_0, not_1_out);
  and and_10 (and_10_out, MAR_1, not_1_out);
  and and_11 (and_11_out, MAR_2, not_1_out);
  and and_12 (and_12_out, MAR_3, not_1_out);
  and and_13 (and_13_out, MAR_4, not_1_out);
  and and_14 (and_14_out, MAR_5, not_1_out);
  and and_15 (and_15_out, MAR_6, not_1_out);
  and and_16 (and_16_out, MAR_7, not_1_out);
  and and_17 (and_17_out, DEST_8, DO_JMP);
  and and_18 (and_18_out, DEST_9, DO_JMP);
  and and_19 (and_19_out, DEST_10, DO_JMP);
  and and_20 (and_20_out, DEST_11, DO_JMP);
  and and_21 (and_21_out, RR_0, not_1_out);
  and and_22 (and_22_out, RR_1, not_1_out);
  and and_23 (and_23_out, RR_2, not_1_out);
  and and_24 (and_24_out, RR_3, not_1_out);
  or or_1 (or_1_out, and_17_out, and_21_out);
  or or_2 (or_2_out, and_18_out, and_22_out);
  or or_3 (or_3_out, and_19_out, and_23_out);
  or or_4 (or_4_out, and_20_out, and_24_out);
  or or_5 (or_5_out, and_1_out, and_9_out);
  or or_6 (or_6_out, and_2_out, and_10_out);
  or or_7 (or_7_out, and_3_out, and_11_out);
  or or_8 (or_8_out, and_4_out, and_12_out);
  or or_9 (or_9_out, and_5_out, and_13_out);
  or or_10 (or_10_out, and_6_out, and_14_out);
  or or_11 (or_11_out, and_7_out, and_15_out);
  or or_12 (or_12_out, and_8_out, and_16_out);
  not not_2 (not_2_out, O_S);
  and and_25 (and_25_out, or_5_out, not_2_out);
  and and_26 (and_26_out, or_6_out, not_2_out);
  and and_27 (and_27_out, or_7_out, not_2_out);
  and and_28 (and_28_out, or_8_out, not_2_out);
  and and_29 (and_29_out, or_9_out, not_2_out);
  and and_30 (and_30_out, or_10_out, not_2_out);
  and and_31 (and_31_out, or_11_out, not_2_out);
  and and_32 (and_32_out, or_12_out, not_2_out);
  and and_33 (and_33_out, or_1_out, O_S);
  and and_34 (and_34_out, or_2_out, O_S);
  and and_35 (and_35_out, or_3_out, O_S);
  and and_36 (and_36_out, or_4_out, O_S);
  and and_37 (and_37_out, MAR, O_S);
  and and_38 (and_38_out, WRITE, O_S);
  and and_39 (and_39_out, JMP, O_S);
  and and_40 (and_40_out, F_I, O_S);
  or or_13 (OUT_0, and_25_out, and_33_out);
  or or_14 (OUT_1, and_26_out, and_34_out);
  or or_15 (OUT_2, and_27_out, and_35_out);
  or or_16 (OUT_3, and_28_out, and_36_out);
  or or_17 (OUT_4, and_29_out, and_37_out);
  or or_18 (OUT_5, and_30_out, and_38_out);
  or or_19 (OUT_6, and_31_out, and_39_out);
  or or_20 (OUT_7, and_32_out, and_40_out);
endmodule

module inst_dec (
  input  D0,
  input  D1,
  input  D2,
  input  D3,
  input  CLK1,
  input  RST_C,
  output SMH,
  output LOG,
  output LD,
  output STR,
  output SEI,
  output SML,
  output ARI,
  output W_CAR,
  output I0,
  output I1,
  output I2,
  output I3,
  output JMP,
  output LDD
);

  wire and_1_out, and_2_out, and_8_out, and_10_out, and_13_out, and_15_out, and_17_out, d_ff_1_qn, d_ff_2_qn,
       d_ff_3_qn, d_ff_4_qn, nand_1_out, nor_1_out, not_1_out, not_2_out, or_1_out;

  D_Flip_Flop d_ff_1 (.D(D0), .clk(CLK1), .Q(I0), .Qn(d_ff_1_qn), .reset(RST_C));  // open: preset
  D_Flip_Flop d_ff_2 (.D(D1), .clk(CLK1), .Q(I1), .Qn(d_ff_2_qn), .reset(RST_C));  // open: preset
  D_Flip_Flop d_ff_3 (.D(D2), .clk(CLK1), .Q(I2), .Qn(d_ff_3_qn), .reset(RST_C));  // open: preset
  D_Flip_Flop d_ff_4 (.D(D3), .clk(CLK1), .Q(I3), .Qn(d_ff_4_qn), .reset(RST_C));  // open: preset
  and and_1 (and_1_out, d_ff_4_qn, I2);
  and and_2 (and_2_out, I0, I1);
  and and_3 (ARI, d_ff_3_qn, I3);
  nand nand_1 (nand_1_out, I0, I1);
  and and_4 (W_CAR, ARI, I1);
  not not_1 (not_1_out, and_2_out);
  and and_5 (JMP, and_1_out, not_1_out);
  and and_6 (LDD, and_2_out, and_1_out);
  and and_7 (LOG, nand_1_out, or_1_out);
  or or_1 (or_1_out, and_8_out, LD);
  and and_8 (and_8_out, I2, I3);
  and and_9 (SMH, not_2_out, or_1_out);
  not not_2 (not_2_out, nand_1_out);
  nor nor_1 (nor_1_out, I2, I3);
  and and_10 (and_10_out, d_ff_1_qn, d_ff_2_qn);
  and and_11 (LD, and_10_out, nor_1_out);
  and and_12 (STR, and_13_out, nor_1_out);
  and and_13 (and_13_out, I0, d_ff_2_qn);
  and and_14 (SEI, and_15_out, nor_1_out);
  and and_15 (and_15_out, d_ff_1_qn, I1);
  and and_16 (SML, and_17_out, nor_1_out);
  and and_17 (and_17_out, I0, I1);
endmodule

module test_board (
);

  wire CPU_1_o_4_mar, CPU_1_o_5_write, CPU_1_o_6_jmp, CPU_1_o_7_i, DipSwitch_1_sw7, n7400_1_pin4,
       n7400_1_pin6, n7400_1_pin8, n7400_1_pin10, n7400_1_pin11, n7400_1_pin13, n7408_1_pin3, n7408_1_pin8,
       n7408_2_pin11, n7432_1_pin11, n7432_1_pin12, n7432_1_pin13, n7474_1_pin2, n7474_1_pin4, n7474_1_pin5,
       n7474_1_pin9, n7474_1_pin10, n7474_1_pin12, n7474_2_pin4, n7474_2_pin10, n74163_1_pin1, n74163_1_pin2,
       n74163_1_pin3, n74163_1_pin4, n74163_1_pin5, n74163_1_pin6, n74163_1_pin7, n74163_1_pin9,
       n74163_1_pin10, n74163_1_pin15, n74163_2_pin3, n74163_2_pin4, n74163_2_pin5, n74163_2_pin6,
       n74163_2_pin15, n74163_3_pin3, n74163_3_pin4, n74163_3_pin5, n74163_3_pin6, n74244_1_pin1,
       n74244_1_pin3, n74244_1_pin5, n74244_1_pin7, n74244_1_pin9, n74244_1_pin19;
  wire [3:0] n74244_2_pin18;
  wire [7:0] n74273_2_pin2, ROM_1_data;
  wire [11:0] n74163_1_pin14;

  _74163 u_74163_1 (
    .pin1(n74163_1_pin1), .pin2(n74163_1_pin2), .pin3(n74163_1_pin3), .pin4(n74163_1_pin4),
    .pin5(n74163_1_pin5), .pin6(n74163_1_pin6), .pin7(n74163_1_pin7), .pin15(n74163_1_pin15),
    .pin14(n74163_1_pin14[0]), .pin13(n74163_1_pin14[1]), .pin12(n74163_1_pin14[2]),
    .pin11(n74163_1_pin14[3]), .pin10(n74163_1_pin10), .pin9(n74163_1_pin9));
  _74163 u_74163_2 (
    .pin1(n74163_1_pin1), .pin2(n74163_1_pin2), .pin3(n74163_2_pin3), .pin4(n74163_2_pin4),
    .pin5(n74163_2_pin5), .pin6(n74163_2_pin6), .pin7(n74163_1_pin7), .pin15(n74163_2_pin15),
    .pin14(n74163_1_pin14[4]), .pin13(n74163_1_pin14[5]), .pin12(n74163_1_pin14[6]),
    .pin11(n74163_1_pin14[7]), .pin10(n74163_1_pin15), .pin9(n74163_1_pin9));
  _74163 u_74163_3 (
    .pin1(n74163_1_pin1), .pin2(n74163_1_pin2), .pin3(n74163_3_pin3), .pin4(n74163_3_pin4),
    .pin5(n74163_3_pin5), .pin6(n74163_3_pin6), .pin7(n74163_1_pin7), .pin14(n74163_1_pin14[8]),
    .pin13(n74163_1_pin14[9]), .pin12(n74163_1_pin14[10]), .pin11(n74163_1_pin14[11]),
    .pin10(n74163_2_pin15), .pin9(n74163_1_pin9));  // open: pin15
  DipSwitch DipSwitch_1 (.sw7(DipSwitch_1_sw7));  // open: sw1, sw2, sw3, sw4, sw5, sw6, sw8
  _7400 u_7400_1 (
    .pin1(DipSwitch_1_sw7), .pin2(DipSwitch_1_sw7), .pin3(n74163_1_pin1), .pin4(n7400_1_pin4),
    .pin5(n7400_1_pin4), .pin6(n7400_1_pin6), .pin13(n7400_1_pin13), .pin12(n7400_1_pin13),
    .pin11(n7400_1_pin11), .pin10(n7400_1_pin10), .pin9(n7400_1_pin10), .pin8(n7400_1_pin8));
  Clock clock_1 (.out(n7400_1_pin4));
  ROM #(.addrWidth(12)) ROM_1 (.addr(n74163_1_pin14), .data(ROM_1_data));
  _7474 u_7474_1 (
    .pin1(n74163_1_pin1), .pin2(n7474_1_pin2), .pin3(n7400_1_pin4), .pin4(n7474_1_pin4), .pin5(n7474_1_pin5),
    .pin6(n7474_1_pin2), .pin13(n74163_1_pin1), .pin12(n7474_1_pin12), .pin11(n7400_1_pin8),
    .pin10(n7474_1_pin10), .pin9(n7474_1_pin9), .pin8(n7474_1_pin12));
  _74244 u_74244_1 (
    .pin1(n74244_1_pin1), .pin2(ROM_1_data[7]), .pin3(n74244_1_pin3), .pin4(ROM_1_data[6]),
    .pin5(n74244_1_pin5), .pin6(ROM_1_data[5]), .pin7(n74244_1_pin7), .pin8(ROM_1_data[4]),
    .pin9(n74244_1_pin9), .pin19(n74244_1_pin19), .pin18(n74244_1_pin3), .pin17(ROM_1_data[3]),
    .pin16(n74244_1_pin5), .pin15(ROM_1_data[2]), .pin14(n74244_1_pin7), .pin13(ROM_1_data[1]),
    .pin12(n74244_1_pin9), .pin11(ROM_1_data[0]));
  _7408 u_7408_1 (
    .pin1(n7474_1_pin5), .pin2(n7400_1_pin6), .pin3(n7408_1_pin3), .pin4(n7400_1_pin10),
    .pin5(n7474_1_pin12), .pin6(n74163_1_pin2), .pin13(n7400_1_pin6), .pin12(n7474_1_pin2),
    .pin11(n7400_1_pin10), .pin10(n7400_1_pin10), .pin9(n7474_1_pin9), .pin8(n7408_1_pin8));
  _7432 u_7432_1 (
    .pin13(n7432_1_pin13), .pin12(n7432_1_pin12), .pin11(n7432_1_pin11));  // open: pin1, pin2, pin3, pin4, pin5, pin6, pin10, pin9, pin8
  CPU CPU_1 (
    .EF0(1'b1), .EF1(1'b1), .D0(n74244_1_pin9), .D1(n74244_1_pin7), .D2(n74244_1_pin5), .D3(n74244_1_pin3),
    .RST(DipSwitch_1_sw7), .CLK(n7400_1_pin4), .O_D0_RR0(n74163_3_pin3), .O_D1_RR1(n74163_3_pin4),
    .O_D2_RR2(n74163_3_pin5), .O_D3_RR3(n74163_3_pin6), .O_4_MAR(CPU_1_o_4_mar), .O_5_WRITE(CPU_1_o_5_write),
    .O_6_JMP(CPU_1_o_6_jmp), .O_7_I(CPU_1_o_7_i));
  _7408 u_7408_2 (
    .pin13(n74163_1_pin2), .pin12(CPU_1_o_4_mar), .pin11(n7408_2_pin11), .pin10(CPU_1_o_5_write),
    .pin9(n74163_1_pin2), .pin8(n7400_1_pin13));  // open: pin1, pin2, pin3, pin4, pin5, pin6
  _7400 u_7400_2 (
    .pin1(CPU_1_o_6_jmp), .pin2(CPU_1_o_6_jmp), .pin3(n74163_1_pin9), .pin10(n7432_1_pin13),
    .pin9(n74244_1_pin19), .pin8(n74244_1_pin1));  // open: pin4, pin5, pin6, pin13, pin12, pin11
  _74244 u_74244_2 (
    .pin1(n7400_1_pin11), .pin2(n74163_3_pin3), .pin3(n74244_1_pin9), .pin4(n74163_3_pin4),
    .pin5(n74244_1_pin7), .pin6(n74163_3_pin5), .pin7(n74244_1_pin5), .pin8(n74163_3_pin6),
    .pin9(n74244_1_pin3), .pin19(n7432_1_pin11), .pin18(n74244_2_pin18[0]), .pin17(n74244_2_pin18[0]),
    .pin16(n74244_2_pin18[1]), .pin15(n74244_2_pin18[1]), .pin14(n74244_2_pin18[2]),
    .pin13(n74244_2_pin18[2]), .pin12(n74244_2_pin18[3]), .pin11(n74244_2_pin18[3]));
  _7474 u_7474_2 (
    .pin1(n74163_1_pin1), .pin2(CPU_1_o_7_i), .pin3(n74163_1_pin2), .pin4(n7474_2_pin4),
    .pin5(n7432_1_pin13), .pin13(n74163_1_pin1), .pin12(n7432_1_pin12), .pin11(n7408_1_pin3),
    .pin10(n7474_2_pin10), .pin9(n74244_1_pin19), .pin8(n7432_1_pin12));  // open: pin6
  _74273 u_74273_1 (
    .pin1(n74163_1_pin1), .pin2(n74163_1_pin3), .pin3(n74163_3_pin3), .pin4(n74163_3_pin4),
    .pin5(n74163_1_pin4), .pin6(n74163_1_pin5), .pin7(n74163_3_pin5), .pin8(n74163_3_pin6),
    .pin9(n74163_1_pin6), .pin19(n74163_2_pin6), .pin18(CPU_1_o_7_i), .pin17(CPU_1_o_6_jmp),
    .pin16(n74163_2_pin5), .pin15(n74163_2_pin4), .pin14(CPU_1_o_5_write), .pin13(CPU_1_o_4_mar),
    .pin12(n74163_2_pin3), .pin11(n7408_1_pin8));
  Pull_Resistor pull_resistor_1 (.node(n74244_2_pin18[0]));
  Pull_Resistor pull_resistor_2 (.node(n74244_2_pin18[1]));
  Pull_Resistor pull_resistor_3 (.node(n74244_2_pin18[2]));
  Pull_Resistor pull_resistor_4 (.node(n74244_2_pin18[3]));
  RAM #(.dataWidth(4), .databus("bidir")) RAM_1 (
    .addr(n74273_2_pin2), .we(n7400_1_pin13), .oe(n7400_1_pin11), .clk(n7400_1_pin4), .data(n74244_2_pin18));
  _74273 u_74273_2 (
    .pin1(n74163_1_pin1), .pin2(n74273_2_pin2[0]), .pin3(n74163_1_pin3), .pin4(n74163_1_pin4),
    .pin5(n74273_2_pin2[1]), .pin6(n74273_2_pin2[2]), .pin7(n74163_1_pin5), .pin8(n74163_1_pin6),
    .pin9(n74273_2_pin2[3]), .pin19(n74273_2_pin2[7]), .pin18(n74163_2_pin6), .pin17(n74163_2_pin5),
    .pin16(n74273_2_pin2[6]), .pin15(n74273_2_pin2[5]), .pin14(n74163_2_pin4), .pin13(n74163_2_pin3),
    .pin12(n74273_2_pin2[4]), .pin11(n7408_2_pin11));
  // also tied to VCC on the sheet: {n74163_1_pin7, n74163_1_pin10, n7474_1_pin4, n7474_1_pin10, n7474_2_pin4, n7474_2_pin10}

  // Notes on the sheet:
  //   contents of ROM_1 (hex, n*v repeats v):
  //   2 2 3f 2 13 2 10 1 2 13 0 2 68 1 2 3 0 2 a 1 2 87 7 7 4
endmodule

module shift_reg (
  input  D0,
  input  D1,
  input  D2,
  input  D3,
  input  SHIFT,
  input  LOAD,
  output Q0,
  output Q1,
  output Q2,
  output Q3
);

  wire and_1_out, and_2_out, and_3_out, and_4_out, and_5_out, and_6_out, and_7_out, and_8_out, d_ff_1_qn,
       d_ff_2_qn, d_ff_3_qn, not_1_out, not_2_out, not_3_out, not_4_out, not_5_out, not_6_out, not_7_out;

  D_Flip_Flop d_ff_1 (.D(1'b0), .clk(SHIFT), .Q(Q0), .Qn(d_ff_1_qn), .preset(and_1_out), .reset(and_2_out));
  not not_1 (not_1_out, D0);
  and and_1 (and_1_out, D0, LOAD);
  and and_2 (and_2_out, not_1_out, LOAD);
  not not_2 (not_2_out, d_ff_1_qn);
  and and_3 (and_3_out, D1, LOAD);
  D_Flip_Flop d_ff_2 (.D(not_2_out), .clk(SHIFT), .Q(Q1), .Qn(d_ff_2_qn), .preset(and_3_out), .reset(and_4_out));
  and and_4 (and_4_out, not_3_out, LOAD);
  not not_3 (not_3_out, D1);
  not not_4 (not_4_out, d_ff_2_qn);
  and and_5 (and_5_out, D2, LOAD);
  D_Flip_Flop d_ff_3 (.D(not_4_out), .clk(SHIFT), .Q(Q2), .Qn(d_ff_3_qn), .preset(and_5_out), .reset(and_6_out));
  and and_6 (and_6_out, not_5_out, LOAD);
  not not_5 (not_5_out, D2);
  not not_6 (not_6_out, d_ff_3_qn);
  and and_7 (and_7_out, D3, LOAD);
  D_Flip_Flop d_ff_4 (.D(not_6_out), .clk(SHIFT), .Q(Q3), .preset(and_7_out), .reset(and_8_out));  // open: Qn
  and and_8 (and_8_out, not_7_out, LOAD);
  not not_7 (not_7_out, D3);
endmodule

module adder_8bit (
  input  A0,
  input  A1,
  input  A2,
  input  A3,
  input  A4,
  input  A5,
  input  A6,
  input  A7,
  input  B0,
  input  B1,
  input  B2,
  input  B3,
  input  B4,
  input  B5,
  input  B6,
  input  B7,
  output R0,
  output R1,
  output R2,
  output R3,
  output R4,
  output R5,
  output R6,
  output R7
);

  wire and_1_out, and_2_out, and_3_out, and_4_out, and_5_out, and_6_out, and_7_out, and_8_out, and_9_out,
       and_10_out, and_11_out, and_12_out, and_13_out, and_14_out, or_1_out, or_2_out, or_3_out, or_4_out,
       or_5_out, or_6_out, or_7_out, xor_1_out, xor_2_out, xor_3_out, xor_4_out, xor_5_out, xor_6_out,
       xor_7_out, xor_8_out;

  xor xor_1 (xor_1_out, A0, B0);
  xor xor_2 (xor_2_out, A1, B1);
  xor xor_3 (xor_3_out, A2, B2);
  xor xor_4 (xor_4_out, A3, B3);
  xor xor_5 (xor_5_out, A4, B4);
  xor xor_6 (xor_6_out, A5, B5);
  xor xor_7 (xor_7_out, A6, B6);
  xor xor_8 (xor_8_out, A7, B7);
  xor xor_9 (R0, xor_1_out, 1'b0);
  and and_1 (and_1_out, xor_1_out, 1'b0);
  and and_2 (and_2_out, A0, B0);
  xor xor_10 (R1, xor_2_out, or_1_out);
  and and_3 (and_3_out, xor_2_out, or_1_out);
  and and_4 (and_4_out, A1, B1);
  xor xor_11 (R2, xor_3_out, or_2_out);
  and and_5 (and_5_out, xor_3_out, or_2_out);
  and and_6 (and_6_out, A2, B2);
  xor xor_12 (R3, xor_4_out, or_3_out);
  and and_7 (and_7_out, xor_4_out, or_3_out);
  and and_8 (and_8_out, A3, B3);
  xor xor_13 (R4, xor_5_out, or_4_out);
  and and_9 (and_9_out, xor_5_out, or_4_out);
  and and_10 (and_10_out, A4, B4);
  xor xor_14 (R5, xor_6_out, or_5_out);
  and and_11 (and_11_out, xor_6_out, or_5_out);
  and and_12 (and_12_out, A5, B5);
  xor xor_15 (R6, xor_7_out, or_6_out);
  and and_13 (and_13_out, xor_7_out, or_6_out);
  and and_14 (and_14_out, A6, B6);
  xor xor_16 (R7, xor_8_out, or_7_out);
  or or_1 (or_1_out, and_1_out, and_2_out);
  or or_2 (or_2_out, and_3_out, and_4_out);
  or or_3 (or_3_out, and_5_out, and_6_out);
  or or_4 (or_4_out, and_7_out, and_8_out);
  or or_5 (or_5_out, and_9_out, and_10_out);
  or or_6 (or_6_out, and_11_out, and_12_out);
  or or_7 (or_7_out, and_13_out, and_14_out);
endmodule

module shift_reg_8 (
  input  D0,
  input  D1,
  input  D2,
  input  D3,
  input  SHIFT,
  input  LOAD,
  output Q0,
  output Q1,
  output Q2,
  output Q3,
  output Q4,
  output Q5,
  output Q6,
  output Q7
);

  wire and_1_out, and_2_out, and_3_out, and_4_out, and_5_out, and_6_out, and_7_out, and_8_out, d_ff_1_qn,
       d_ff_2_qn, d_ff_3_qn, d_ff_4_qn, d_ff_5_qn, d_ff_6_qn, d_ff_7_qn, not_1_out, not_2_out, not_3_out,
       not_4_out, not_5_out, not_6_out, not_7_out, not_8_out, not_9_out, not_10_out, not_11_out;

  D_Flip_Flop d_ff_1 (.D(1'b0), .clk(SHIFT), .Q(Q0), .Qn(d_ff_1_qn), .preset(and_1_out), .reset(and_2_out));
  not not_1 (not_1_out, D0);
  and and_1 (and_1_out, D0, LOAD);
  and and_2 (and_2_out, not_1_out, LOAD);
  not not_2 (not_2_out, d_ff_1_qn);
  and and_3 (and_3_out, D1, LOAD);
  D_Flip_Flop d_ff_2 (.D(not_2_out), .clk(SHIFT), .Q(Q1), .Qn(d_ff_2_qn), .preset(and_3_out), .reset(and_4_out));
  and and_4 (and_4_out, not_3_out, LOAD);
  not not_3 (not_3_out, D1);
  not not_4 (not_4_out, d_ff_2_qn);
  and and_5 (and_5_out, D2, LOAD);
  D_Flip_Flop d_ff_3 (.D(not_4_out), .clk(SHIFT), .Q(Q2), .Qn(d_ff_3_qn), .preset(and_5_out), .reset(and_6_out));
  and and_6 (and_6_out, not_5_out, LOAD);
  not not_5 (not_5_out, D2);
  not not_6 (not_6_out, d_ff_3_qn);
  and and_7 (and_7_out, D3, LOAD);
  D_Flip_Flop d_ff_4 (.D(not_6_out), .clk(SHIFT), .Q(Q3), .Qn(d_ff_4_qn), .preset(and_7_out), .reset(and_8_out));
  and and_8 (and_8_out, not_7_out, LOAD);
  not not_7 (not_7_out, D3);
  not not_8 (not_8_out, d_ff_4_qn);
  D_Flip_Flop d_ff_5 (.D(not_8_out), .clk(SHIFT), .Q(Q4), .Qn(d_ff_5_qn), .reset(LOAD));  // open: preset
  D_Flip_Flop d_ff_6 (.D(not_9_out), .clk(SHIFT), .Q(Q5), .Qn(d_ff_6_qn), .reset(LOAD));  // open: preset
  not not_9 (not_9_out, d_ff_5_qn);
  not not_10 (not_10_out, d_ff_6_qn);
  D_Flip_Flop d_ff_7 (.D(not_10_out), .clk(SHIFT), .Q(Q6), .Qn(d_ff_7_qn), .reset(LOAD));  // open: preset
  D_Flip_Flop d_ff_8 (.D(not_11_out), .clk(SHIFT), .Q(Q7), .reset(LOAD));  // open: Qn, preset
  not not_11 (not_11_out, d_ff_7_qn);
endmodule

module dest_reg_sel_new (
  input  CLK1,
  input  LDD,
  input  RST,
  output S0,
  output S1,
  output S2
);

  wire and_1_out, and_2_out, and_3_out, and_4_out, and_5_out, and_6_out, and_7_out, and_8_out, and_9_out,
       and_10_out, and_11_out, and_12_out, and_13_out, and_14_out, and_15_out, and_16_out, and_17_out,
       and_18_out, not_1_out, not_2_out, not_3_out, not_4_out, not_5_out, not_6_out, or_1_out, or_2_out,
       or_3_out, or_4_out, or_5_out, or_6_out, or_7_out, or_8_out;

  not not_1 (not_1_out, CLK1);
  and and_1 (and_1_out, not_1_out, LDD);
  not not_2 (not_2_out, and_1_out);
  not not_3 (not_3_out, S1);
  not not_4 (not_4_out, or_7_out);
  and and_2 (and_2_out, not_4_out, not_6_out);
  and and_3 (and_3_out, not_6_out, S1);
  and and_4 (and_4_out, not_4_out, not_6_out);
  and and_5 (and_5_out, S1, not_6_out);
  and and_6 (and_6_out, or_7_out, not_3_out);
  and and_7 (and_7_out, or_7_out, not_3_out);
  and and_8 (and_8_out, or_8_out, not_3_out);
  and and_9 (and_9_out, or_8_out, or_7_out);
  and and_10 (and_10_out, and_2_out, and_1_out);
  and and_11 (and_11_out, and_3_out, not_2_out);
  and and_12 (and_12_out, and_4_out, S1);
  and and_13 (and_13_out, and_5_out, not_2_out);
  and and_14 (and_14_out, not_6_out, or_7_out);
  and and_15 (and_15_out, and_6_out, not_2_out);
  and and_16 (and_16_out, and_7_out, not_2_out);
  and and_17 (and_17_out, and_8_out, and_1_out);
  and and_18 (and_18_out, and_9_out, not_3_out);
  or or_1 (or_1_out, and_10_out, and_11_out);
  or or_2 (or_2_out, and_13_out, and_14_out);
  or or_3 (or_3_out, and_16_out, and_17_out);
  or or_4 (or_4_out, or_1_out, and_12_out);
  or or_5 (or_5_out, or_2_out, and_15_out);
  or or_6 (or_6_out, or_3_out, and_18_out);
  not not_5 (not_5_out, RST);
  or or_7 (or_7_out, RST, or_5_out);
  and and_19 (S1, not_5_out, or_4_out);
  or or_8 (or_8_out, RST, or_6_out);
  not not_6 (not_6_out, or_8_out);
  and and_20 (S0, not_3_out, not_4_out);
  and and_21 (S2, not_3_out, or_7_out);
endmodule

module clock_gen_2 (
  input  RST,
  input  CLK,
  input  RST_C,
  output O_S,
  output CLK1,
  output CLK2
);

  wire d_ff_1_q, d_ff_1_qn, d_ff_2_q, d_ff_2_qn, d_ff_3_qn, or_1_out;

  D_Flip_Flop d_ff_1 (.D(d_ff_1_qn), .clk(CLK), .Q(d_ff_1_q), .Qn(d_ff_1_qn), .reset(RST_C));  // open: preset
  D_Flip_Flop d_ff_2 (.D(d_ff_2_qn), .clk(d_ff_1_qn), .Q(d_ff_2_q), .Qn(d_ff_2_qn), .reset(RST_C));  // open: preset
  and and_1 (CLK1, d_ff_1_q, d_ff_2_qn);
  and and_2 (CLK2, d_ff_1_q, d_ff_2_q);
  D_Flip_Flop d_ff_3 (.D(d_ff_3_qn), .clk(or_1_out), .Q(O_S), .Qn(d_ff_3_qn), .preset(RST_C));  // open: reset
  or or_1 (or_1_out, CLK1, CLK2);
endmodule

module int_memory (
  input  ADR0,
  input  ADR1,
  input  ADR2,
  input  ADR3,
  input  DI0,
  input  DI1,
  input  DI2,
  input  DI3,
  input  EN,
  input  WR,
  input  CLK,
  output DO0,
  output DO1,
  output DO2,
  output DO3
);

  wire and_1_out, and_2_out, and_3_out, and_4_out, and_5_out, and_6_out, and_7_out, and_8_out, and_9_out,
       and_10_out, and_11_out, and_12_out, and_13_out, and_14_out, and_15_out, and_16_out;
  wire [3:0] and_17_out, and_18_out, and_19_out, and_20_out, and_21_out, and_22_out, and_23_out, and_24_out,
       and_25_out, and_26_out, and_27_out, and_28_out, and_29_out, and_30_out, and_31_out, div_1_m0,
       div_1_r0, div_1_r4, mul2_1_r0, mul2_1_r4, or_1_out, or_2_out, or_3_out, or_4_out, or_5_out,
       register_1_q, register_2_q, register_3_q, register_4_q, register_5_q, register_6_q, register_7_q,
       register_8_q, register_9_q, register_10_q, register_11_q, register_12_q, register_13_q, register_14_q,
       register_15_q;
  wire [3:3] demultiplexer_1_out0, demultiplexer_1_out1, demultiplexer_1_out2, demultiplexer_1_out3,
       demultiplexer_1_out4, demultiplexer_1_out5, demultiplexer_1_out6, demultiplexer_1_out7,
       demultiplexer_1_out8, demultiplexer_1_out9, demultiplexer_1_out10, demultiplexer_1_out11,
       demultiplexer_1_out12, demultiplexer_1_out13, demultiplexer_1_out14;

  Demultiplexer #(.select(4)) demultiplexer_1 (
    .out0(demultiplexer_1_out0[3]), .out1(demultiplexer_1_out1[3]), .out2(demultiplexer_1_out2[3]),
    .out3(demultiplexer_1_out3[3]), .out4(demultiplexer_1_out4[3]), .out5(demultiplexer_1_out5[3]),
    .out6(demultiplexer_1_out6[3]), .out7(demultiplexer_1_out7[3]), .out8(demultiplexer_1_out8[3]),
    .out9(demultiplexer_1_out9[3]), .out10(demultiplexer_1_out10[3]), .out11(demultiplexer_1_out11[3]),
    .out12(demultiplexer_1_out12[3]), .out13(demultiplexer_1_out13[3]), .out14(demultiplexer_1_out14[3]),
    .in(1'b1), .sel({ADR3, ADR2, ADR1, ADR0}));  // open: out15
  and and_1 (and_1_out, EN, CLK);
  and and_2 (and_2_out, and_1_out, demultiplexer_1_out0[3]);
  and and_3 (and_3_out, and_1_out, demultiplexer_1_out1[3]);
  and and_4 (and_4_out, and_1_out, demultiplexer_1_out2[3]);
  and and_5 (and_5_out, and_1_out, demultiplexer_1_out3[3]);
  and and_6 (and_6_out, and_1_out, demultiplexer_1_out4[3]);
  and and_7 (and_7_out, and_1_out, demultiplexer_1_out5[3]);
  and and_8 (and_8_out, and_1_out, demultiplexer_1_out6[3]);
  and and_9 (and_9_out, and_1_out, demultiplexer_1_out7[3]);
  and and_10 (and_10_out, and_1_out, demultiplexer_1_out10[3]);
  and and_11 (and_11_out, and_1_out, demultiplexer_1_out11[3]);
  and and_12 (and_12_out, and_1_out, demultiplexer_1_out12[3]);
  and and_13 (and_13_out, and_1_out, demultiplexer_1_out13[3]);
  and and_14 (and_14_out, and_1_out, demultiplexer_1_out14[3]);
  and and_15 (and_15_out, and_1_out, demultiplexer_1_out8[3]);
  and and_16 (and_16_out, and_1_out, demultiplexer_1_out9[3]);
  Register #(.width(4)) register_1 (.D({DI3, DI2, DI1, DI0}), .en(WR), .clk(and_2_out), .Q(register_1_q));  // open: clr
  Register #(.width(4)) register_2 (.D({DI3, DI2, DI1, DI0}), .en(WR), .clk(and_3_out), .Q(register_2_q));  // open: clr
  Register #(.width(4)) register_3 (.D({DI3, DI2, DI1, DI0}), .en(WR), .clk(and_4_out), .Q(register_3_q));  // open: clr
  Register #(.width(4)) register_4 (.D({DI3, DI2, DI1, DI0}), .en(WR), .clk(and_5_out), .Q(register_4_q));  // open: clr
  Register #(.width(4)) register_5 (.D({DI3, DI2, DI1, DI0}), .en(WR), .clk(and_6_out), .Q(register_5_q));  // open: clr
  Register #(.width(4)) register_6 (.D({DI3, DI2, DI1, DI0}), .en(WR), .clk(and_7_out), .Q(register_6_q));  // open: clr
  Register #(.width(4)) register_7 (.D({DI3, DI2, DI1, DI0}), .en(WR), .clk(and_8_out), .Q(register_7_q));  // open: clr
  Register #(.width(4)) register_8 (.D({DI3, DI2, DI1, DI0}), .en(WR), .clk(and_9_out), .Q(register_8_q));  // open: clr
  Register #(.width(4)) register_9 (
    .D({DI3, DI2, DI1, DI0}), .en(WR), .clk(and_10_out), .Q(register_9_q));  // open: clr
  Register #(.width(4)) register_10 (
    .D({DI3, DI2, DI1, DI0}), .en(WR), .clk(and_11_out), .Q(register_10_q));  // open: clr
  Register #(.width(4)) register_11 (
    .D({DI3, DI2, DI1, DI0}), .en(WR), .clk(and_12_out), .Q(register_11_q));  // open: clr
  Register #(.width(4)) register_12 (
    .D({DI3, DI2, DI1, DI0}), .en(WR), .clk(and_13_out), .Q(register_12_q));  // open: clr
  Register #(.width(4)) register_13 (
    .D({DI3, DI2, DI1, DI0}), .en(WR), .clk(and_14_out), .Q(register_13_q));  // open: clr
  Register #(.width(4)) register_14 (
    .D({DI3, DI2, DI1, DI0}), .en(WR), .clk(and_15_out), .Q(register_14_q));  // open: clr
  Register #(.width(4)) register_15 (
    .D({DI3, DI2, DI1, DI0}), .en(WR), .clk(and_16_out), .Q(register_15_q));  // open: clr
  assign and_17_out = {4{demultiplexer_1_out0[3]}} & register_1_q;  // AND_Gate and_17, 4 bits wide
  assign and_18_out = {4{demultiplexer_1_out1[3]}} & register_2_q;  // AND_Gate and_18, 4 bits wide
  assign and_19_out = {4{demultiplexer_1_out2[3]}} & register_3_q;  // AND_Gate and_19, 4 bits wide
  assign and_20_out = {4{demultiplexer_1_out3[3]}} & register_4_q;  // AND_Gate and_20, 4 bits wide
  assign and_21_out = {4{demultiplexer_1_out4[3]}} & register_5_q;  // AND_Gate and_21, 4 bits wide
  assign and_22_out = {4{demultiplexer_1_out5[3]}} & register_6_q;  // AND_Gate and_22, 4 bits wide
  assign and_23_out = {4{demultiplexer_1_out6[3]}} & register_7_q;  // AND_Gate and_23, 4 bits wide
  assign and_24_out = {4{demultiplexer_1_out7[3]}} & register_8_q;  // AND_Gate and_24, 4 bits wide
  assign and_25_out = {4{demultiplexer_1_out8[3]}} & register_14_q;  // AND_Gate and_25, 4 bits wide
  assign and_26_out = {4{demultiplexer_1_out9[3]}} & register_15_q;  // AND_Gate and_26, 4 bits wide
  mul2 mul2_1 (
    .A0(register_9_q[0]), .A1(register_9_q[1]), .A2(register_9_q[2]), .A3(register_9_q[3]),
    .B0(register_10_q[0]), .B1(register_10_q[1]), .B2(register_10_q[2]), .B3(register_10_q[3]),
    .R0(mul2_1_r0[0]), .R1(mul2_1_r0[1]), .R2(mul2_1_r0[2]), .R3(mul2_1_r0[3]), .R4(mul2_1_r4[0]),
    .R5(mul2_1_r4[1]), .R6(mul2_1_r4[2]), .R7(mul2_1_r4[3]));
  div div_1 (
    .A0(register_11_q[0]), .A1(register_11_q[1]), .A2(register_11_q[2]), .A3(register_11_q[3]),
    .A4(register_12_q[0]), .A5(register_12_q[1]), .A6(register_12_q[2]), .A7(register_12_q[3]),
    .B0(register_13_q[0]), .B1(register_13_q[1]), .B2(register_13_q[2]), .B3(register_13_q[3]),
    .M0(div_1_m0[0]), .M1(div_1_m0[1]), .M2(div_1_m0[2]), .M3(div_1_m0[3]), .R0(div_1_r0[0]),
    .R1(div_1_r0[1]), .R2(div_1_r0[2]), .R3(div_1_r0[3]), .R4(div_1_r4[0]), .R5(div_1_r4[1]),
    .R6(div_1_r4[2]), .R7(div_1_r4[3]));
  assign or_1_out = and_17_out | and_18_out | and_19_out | and_20_out;  // OR_Gate or_1, 4 bits wide
  assign or_2_out = and_21_out | and_22_out | and_23_out | and_24_out;  // OR_Gate or_2, 4 bits wide
  assign and_27_out = {4{demultiplexer_1_out10[3]}} & mul2_1_r0;  // AND_Gate and_27, 4 bits wide
  assign and_28_out = {4{demultiplexer_1_out11[3]}} & mul2_1_r4;  // AND_Gate and_28, 4 bits wide
  assign and_29_out = {4{demultiplexer_1_out12[3]}} & div_1_m0;  // AND_Gate and_29, 4 bits wide
  assign and_30_out = {4{demultiplexer_1_out13[3]}} & div_1_r0;  // AND_Gate and_30, 4 bits wide
  assign and_31_out = {4{demultiplexer_1_out14[3]}} & div_1_r4;  // AND_Gate and_31, 4 bits wide
  assign or_3_out = or_1_out | or_2_out | or_4_out;  // OR_Gate or_3, 4 bits wide
  assign {DO3, DO2, DO1, DO0} = or_3_out & {4{EN}};  // AND_Gate and_32, 4 bits wide
  assign or_4_out = and_27_out | and_28_out | or_5_out | and_26_out;  // OR_Gate or_4, 4 bits wide
  assign or_5_out = and_29_out | and_30_out | and_31_out | and_25_out;  // OR_Gate or_5, 4 bits wide
endmodule

module mul2 (
  input  A0,
  input  A1,
  input  A2,
  input  A3,
  input  B0,
  input  B1,
  input  B2,
  input  B3,
  output R0,
  output R1,
  output R2,
  output R3,
  output R4,
  output R5,
  output R6,
  output R7
);

  wire [5:0] adder_1_out, and_1_out, and_2_out;
  wire [7:0] adder_2_out, and_3_out, and_4_out;

  assign and_1_out = {2'b00, A3, A2, A1, A0} & {6{B0}};  // AND_Gate and_1, 6 bits wide
  assign and_2_out = {1'b0, A3, A2, A1, A0, 1'b0} & {6{B1}};  // AND_Gate and_2, 6 bits wide
  assign and_3_out = {2'b00, A3, A2, A1, A0, 2'b00} & {8{B2}};  // AND_Gate and_3, 8 bits wide
  assign and_4_out = {1'b0, A3, A2, A1, A0, 3'b000} & {8{B3}};  // AND_Gate and_4, 8 bits wide
  Adder #(.width(6)) adder_1 (.a(and_1_out), .b(and_2_out), .out(adder_1_out));  // open: cin, cout
  Adder adder_2 (.a({2'b00, adder_1_out}), .b(and_3_out), .out(adder_2_out));  // open: cin, cout
  Adder adder_3 (.a(adder_2_out), .b(and_4_out), .out({R7, R6, R5, R4, R3, R2, R1, R0}));  // open: cin, cout
endmodule

module div (
  input  A0,
  input  A1,
  input  A2,
  input  A3,
  input  A4,
  input  A5,
  input  A6,
  input  A7,
  input  B0,
  input  B1,
  input  B2,
  input  B3,
  output M0,
  output M1,
  output M2,
  output M3,
  output R0,
  output R1,
  output R2,
  output R3,
  output R4,
  output R5,
  output R6,
  output R7
);

  wire comparator_1_eq, comparator_1_gt, comparator_2_eq, comparator_2_gt, comparator_3_eq, comparator_3_gt,
       comparator_4_eq, comparator_4_gt, comparator_5_eq, comparator_5_gt, comparator_6_eq, comparator_6_gt,
       comparator_7_eq, comparator_7_gt, comparator_8_eq, comparator_8_gt, nand_1_out;
  wire [1:0] adder_2_out, nand_2_out;
  wire [1:1] adder_1_out;
  wire [2:0] adder_3_out, nand_3_out;
  wire [4:0] adder_4_out, adder_5_out, adder_6_out, adder_7_out, nand_4_out, nand_5_out, nand_6_out,
       nand_7_out, nand_8_out;
  wire [4:4] adder_8_out;

  Comparator #(.mode("unsigned"), .width(5)) comparator_1 (
    .a({4'b0000, A7}), .b({1'b0, B3, B2, B1, B0}), .gt(comparator_1_gt), .eq(comparator_1_eq));  // open: lt
  or or_1 (R7, comparator_1_gt, comparator_1_eq);
  Adder #(.width(1)) adder_1 (.a(A7), .b(nand_1_out), .out(adder_1_out[1]), .cin(1'b1));  // open: cout
  nand nand_1 (nand_1_out, R7, B0);
  Comparator #(.mode("unsigned"), .width(5)) comparator_2 (
    .a({3'b000, adder_1_out[1], A6}), .b({1'b0, B3, B2, B1, B0}), .gt(comparator_2_gt), .eq(comparator_2_eq));  // open: lt
  or or_2 (R6, comparator_2_gt, comparator_2_eq);
  assign nand_2_out = ~({2{R6}} & {B1, B0});  // NAND_Gate nand_2, 2 bits wide
  Adder #(.width(2)) adder_2 (.a({adder_1_out[1], A6}), .b(nand_2_out), .out(adder_2_out), .cin(1'b1));  // open: cout
  Comparator #(.mode("unsigned"), .width(5)) comparator_3 (
    .a({2'b00, adder_2_out, A5}), .b({1'b0, B3, B2, B1, B0}), .gt(comparator_3_gt), .eq(comparator_3_eq));  // open: lt
  or or_3 (R5, comparator_3_gt, comparator_3_eq);
  assign nand_3_out = ~({3{R5}} & {B2, B1, B0});  // NAND_Gate nand_3, 3 bits wide
  Adder #(.width(3)) adder_3 (.a({adder_2_out, A5}), .b(nand_3_out), .out(adder_3_out), .cin(1'b1));  // open: cout
  Comparator #(.mode("unsigned"), .width(5)) comparator_4 (
    .a({1'b0, adder_3_out, A4}), .b({1'b0, B3, B2, B1, B0}), .gt(comparator_4_gt), .eq(comparator_4_eq));  // open: lt
  or or_4 (R4, comparator_4_gt, comparator_4_eq);
  assign nand_4_out = ~({5{R4}} & {1'b0, B3, B2, B1, B0});  // NAND_Gate nand_4, 5 bits wide
  // NoConnect on adder_4_out[4]
  Adder #(.width(5)) adder_4 (
    .a({1'b0, adder_3_out, A4}), .b(nand_4_out), .out(adder_4_out), .cin(1'b1));  // open: cout
  Comparator #(.mode("unsigned"), .width(5)) comparator_5 (
    .a({adder_4_out[3:0], A3}), .b({1'b0, B3, B2, B1, B0}), .gt(comparator_5_gt), .eq(comparator_5_eq));  // open: lt
  or or_5 (R3, comparator_5_gt, comparator_5_eq);
  assign nand_5_out = ~({5{R3}} & {1'b0, B3, B2, B1, B0});  // NAND_Gate nand_5, 5 bits wide
  // NoConnect on adder_5_out[4]
  Adder #(.width(5)) adder_5 (.a({adder_4_out[3:0], A3}), .b(nand_5_out), .out(adder_5_out), .cin(1'b1));  // open: cout
  Comparator #(.mode("unsigned"), .width(5)) comparator_6 (
    .a({adder_5_out[3:0], A2}), .b({1'b0, B3, B2, B1, B0}), .gt(comparator_6_gt), .eq(comparator_6_eq));  // open: lt
  or or_6 (R2, comparator_6_gt, comparator_6_eq);
  assign nand_6_out = ~({5{R2}} & {1'b0, B3, B2, B1, B0});  // NAND_Gate nand_6, 5 bits wide
  // NoConnect on adder_6_out[4]
  Adder #(.width(5)) adder_6 (.a({adder_5_out[3:0], A2}), .b(nand_6_out), .out(adder_6_out), .cin(1'b1));  // open: cout
  Comparator #(.mode("unsigned"), .width(5)) comparator_7 (
    .a({adder_6_out[3:0], A1}), .b({1'b0, B3, B2, B1, B0}), .gt(comparator_7_gt), .eq(comparator_7_eq));  // open: lt
  or or_7 (R1, comparator_7_gt, comparator_7_eq);
  assign nand_7_out = ~({5{R1}} & {1'b0, B3, B2, B1, B0});  // NAND_Gate nand_7, 5 bits wide
  // NoConnect on adder_7_out[4]
  Adder #(.width(5)) adder_7 (.a({adder_6_out[3:0], A1}), .b(nand_7_out), .out(adder_7_out), .cin(1'b1));  // open: cout
  Comparator #(.mode("unsigned"), .width(5)) comparator_8 (
    .a({adder_7_out[3:0], A0}), .b({1'b0, B3, B2, B1, B0}), .gt(comparator_8_gt), .eq(comparator_8_eq));  // open: lt
  or or_8 (R0, comparator_8_gt, comparator_8_eq);
  assign nand_8_out = ~({5{R0}} & {1'b0, B3, B2, B1, B0});  // NAND_Gate nand_8, 5 bits wide
  Adder #(.width(5)) adder_8 (
    .a({adder_7_out[3:0], A0}), .b(nand_8_out), .out({adder_8_out[4], M3, M2, M1, M0}), .cin(1'b1));  // open: cout
endmodule
